# Fritzing sketch hcs04 (saved by Fritzing 0.9.3b)

parts:
  Mod1 = Raspberry Pi Pico W
  Part1 = SRF05 Ultrasonic Rangefinder

nets:
  N1: Mod1.pin_4, Part1.Trig
  N2: Mod1.pin_5, Part1.Echo
  N3: Mod1.pin_38, Mod1.pin_42, Part1.GND
  N4: Mod1.pin_39, Part1.VCC

custom parts:
  Raspberry Pi Pico W: Raspberry Pi Pico W. Based around the RP2040 microcontroller the Pico W is a low cost microcontroller device bringing Raspberry Pi quality, cost, and easy of use to the microcontroller space. The areas marked KEEPOUT in pcb silkscreen should not have traces running through them to avoid shorts on a soldered in module!
